// Logisim project trab01sistemasdigitaisv2corrigido.circ as structural Verilog: 1 circuit, main circuit main
module main (
  input  cin,
  input  a4,
  input  a3,
  input  a2,
  input  a1,
  input  b4,
  input  b3,
  input  b2,
  input  b1,
  input  s3,
  input  s2,
  input  s1,
  output cout,
  output f4,
  output f3,
  output f2,
  output f1
);

  wire adder_1_cout, adder_1_out, adder_2_cout, adder_2_out, adder_3_cout, adder_3_out, adder_4_out,
       and_1_out, and_2_out, and_3_out, and_4_out, multiplexer_1_out, multiplexer_2_out, multiplexer_3_out,
       multiplexer_4_out, multiplexer_5_out, multiplexer_6_out, multiplexer_7_out, multiplexer_8_out,
       multiplexer_9_out, multiplexer_10_out, multiplexer_11_out, multiplexer_12_out, multiplexer_13_out,
       multiplexer_14_out, multiplexer_15_out, multiplexer_16_out, multiplexer_17_out, multiplexer_18_out,
       multiplexer_19_out, multiplexer_20_out, multiplexer_21_out, multiplexer_22_out, multiplexer_23_out,
       multiplexer_24_out, not_1_out, not_2_out, not_3_out, not_4_out, not_5_out, not_6_out, not_7_out,
       not_8_out, or_1_out, or_2_out, or_3_out, or_4_out, or_5_out, xor_1_out, xor_2_out, xor_3_out,
       xor_4_out, xor_5_out;

  Multiplexer #(.enable("false")) multiplexer_1 (.in0(b1), .in1(not_1_out), .out(multiplexer_1_out), .sel(s1));
  not not_1 (not_1_out, b1);
  Multiplexer #(.enable("false")) multiplexer_2 (.in0(s1), .in1(a1), .out(multiplexer_2_out), .sel(s1));
  Multiplexer #(.enable("false")) multiplexer_3 (.in0(b2), .in1(not_2_out), .out(multiplexer_3_out), .sel(s1));
  not not_2 (not_2_out, b2);
  Multiplexer #(.enable("false")) multiplexer_4 (.in0(s1), .in1(a2), .out(multiplexer_4_out), .sel(s1));
  Multiplexer #(.enable("false")) multiplexer_5 (.in0(b3), .in1(not_3_out), .out(multiplexer_5_out), .sel(s1));
  not not_3 (not_3_out, b3);
  Multiplexer #(.enable("false")) multiplexer_6 (.in0(s1), .in1(a3), .out(multiplexer_6_out), .sel(s1));
  Multiplexer #(.enable("false")) multiplexer_7 (.in0(b4), .in1(not_4_out), .out(multiplexer_7_out), .sel(s1));
  not not_4 (not_4_out, b4);
  Multiplexer #(.enable("false")) multiplexer_8 (.in0(s1), .in1(a4), .out(multiplexer_8_out), .sel(s1));
  or or_1 (or_1_out, b1, a1);
  and and_1 (and_1_out, b1, a1);
  not not_5 (not_5_out, a1);
  xor xor_1 (xor_1_out, b1, a1);
  and and_2 (and_2_out, b2, a2);
  or or_2 (or_2_out, b2, a2);
  not not_6 (not_6_out, a2);
  xor xor_2 (xor_2_out, b2, a2);
  and and_3 (and_3_out, b3, a3);
  or or_3 (or_3_out, b3, a3);
  not not_7 (not_7_out, a3);
  xor xor_3 (xor_3_out, b3, a3);
  and and_4 (and_4_out, b4, a4);
  or or_4 (or_4_out, b4, a4);
  not not_8 (not_8_out, a4);
  xor xor_4 (xor_4_out, b4, a4);
  xor xor_5 (xor_5_out, s2, s1);
  Multiplexer #(.enable("false")) multiplexer_9 (
    .in0(multiplexer_1_out), .in1(multiplexer_2_out), .out(multiplexer_9_out), .sel(s2));
  Multiplexer #(.enable("false")) multiplexer_10 (
    .in0(multiplexer_3_out), .in1(multiplexer_4_out), .out(multiplexer_10_out), .sel(s2));
  Multiplexer #(.enable("false")) multiplexer_11 (
    .in0(multiplexer_5_out), .in1(multiplexer_6_out), .out(multiplexer_11_out), .sel(s2));
  Multiplexer #(.enable("false")) multiplexer_12 (
    .in0(multiplexer_7_out), .in1(multiplexer_8_out), .out(multiplexer_12_out), .sel(s2));
  Multiplexer #(.enable("false")) multiplexer_13 (.in0(and_1_out), .in1(or_1_out), .out(multiplexer_13_out), .sel(s1));
  Multiplexer #(.enable("false")) multiplexer_14 (.in0(not_5_out), .in1(xor_1_out), .out(multiplexer_14_out), .sel(s1));
  Multiplexer #(.enable("false")) multiplexer_15 (.in0(and_2_out), .in1(or_2_out), .out(multiplexer_15_out), .sel(s1));
  Multiplexer #(.enable("false")) multiplexer_16 (.in0(not_6_out), .in1(xor_2_out), .out(multiplexer_16_out), .sel(s1));
  Multiplexer #(.enable("false")) multiplexer_17 (.in0(and_3_out), .in1(or_3_out), .out(multiplexer_17_out), .sel(s1));
  Multiplexer #(.enable("false")) multiplexer_18 (.in0(not_7_out), .in1(xor_3_out), .out(multiplexer_18_out), .sel(s1));
  Multiplexer #(.enable("false")) multiplexer_19 (.in0(and_4_out), .in1(or_4_out), .out(multiplexer_19_out), .sel(s1));
  Multiplexer #(.enable("false")) multiplexer_20 (.in0(not_8_out), .in1(xor_4_out), .out(multiplexer_20_out), .sel(s1));
  Multiplexer #(.enable("false")) multiplexer_21 (
    .in0(multiplexer_13_out), .in1(multiplexer_14_out), .out(multiplexer_21_out), .sel(s2));
  Multiplexer #(.enable("false")) multiplexer_22 (
    .in0(multiplexer_15_out), .in1(multiplexer_16_out), .out(multiplexer_22_out), .sel(s2));
  Multiplexer #(.enable("false")) multiplexer_23 (
    .in0(multiplexer_17_out), .in1(multiplexer_18_out), .out(multiplexer_23_out), .sel(s2));
  Multiplexer #(.enable("false")) multiplexer_24 (
    .in0(multiplexer_19_out), .in1(multiplexer_20_out), .out(multiplexer_24_out), .sel(s2));
  Adder #(.width(1)) adder_1 (.a(a1), .b(multiplexer_9_out), .out(adder_1_out), .cin(xor_5_out), .cout(adder_1_cout));
  Adder #(.width(1)) adder_2 (
    .a(a2), .b(multiplexer_10_out), .out(adder_2_out), .cin(adder_1_cout), .cout(adder_2_cout));
  Adder #(.width(1)) adder_3 (
    .a(a3), .b(multiplexer_11_out), .out(adder_3_out), .cin(adder_2_cout), .cout(adder_3_cout));
  Adder #(.width(1)) adder_4 (.a(a4), .b(multiplexer_12_out), .out(adder_4_out), .cin(adder_3_cout), .cout(cout));
  Multiplexer #(.enable("false")) multiplexer_25 (.in0(adder_1_out), .in1(multiplexer_21_out), .out(f1), .sel(s3));
  Multiplexer #(.enable("false")) multiplexer_26 (.in0(adder_2_out), .in1(multiplexer_22_out), .out(f2), .sel(s3));
  Multiplexer #(.enable("false")) multiplexer_27 (.in0(adder_3_out), .in1(multiplexer_23_out), .out(f3), .sel(s3));
  Multiplexer #(.enable("false")) multiplexer_28 (.in0(adder_4_out), .in1(multiplexer_24_out), .out(f4), .sel(s3));
  // AND_Gate and_5 has open pins: in0=1'b1, out=open
  or or_5 (or_5_out, cin, ~cin);  // OR_Gate

  // Notes on the sheet:
  //   m1
  //   m3
  //   m4
  //   m5
  //   m7
  //   mm1
  //   m2
  //   mm2
  //   mm3
  //   m6
  //   mm4
  //   m8
  //   n1
  //   n2
  //   n3
  //   n4
  //   n5
  //   n6
  //   n7
  //   n8
  //   mmm2
  //   mmm3
  //   mmm4
  //   nn1
  //   nn2
  //   nn3
  //   nn4
  //   mmm1
  //   000 adição
  //   100 and
  //   101 or
  //   110 not
  //   111 xor
  //   tabela de selação das operações
  //   001 subtração
  //   010 incremento (+1)
  //   011 deslocamento de um bit à esquerda
endmodule
